# Fritzing sketch circuit (saved by Fritzing 0.9.4)
breadboards: 1

parts:
  RY1 = SSR-40VA
  Part2 = RFID-RC522-v2
  Part3 = LCD1602-I2C
  S1 = Square Pushbutton
  S2 = Square Pushbutton
  J1 = Piezo Speaker
  Part1 = Arduino Uno (Rev3)
  R1 = Resistor [tolerance=±5% resistance=10k package="0603 [SMD]"]
  R2 = Resistor [tolerance=±5% resistance=10k package="1206 [SMD]"]
  JACK1 = 2.1mm Barrel Jack with Terminal Block
  L1 = Solenoid

nets:
  N1: RY1.Pin_1, L1.pin2
  N2: RY1.Pin_2, JACK1.POS
  N3: RY1.Pin_3, Part1.D2
  GND: RY1.Pin_4, Part2.GND, Part3.GND, S1.leg1, S2.leg1, J1.pin1, Part1.GND, JACK1.NEG, L1.pin1
  N4: Part2.SDA, Part1.D10_PWM/SS
  N5: Part2.SCK, Part1.D13/SCK
  N6: Part2.MOSI, Part1.D11_PWM/MOSI
  N7: Part2.MISO, Part1.D12/MISO
  N8: Part2.RST, Part1.D9_PWM
  3.3V: Part2.3.3V, Part1.3V3
  VCC: Part3.VCC, Part1.5V, R1.Pin_0, R2.Pin_0
  N9: Part3.SDA, Part1.A4/SDA
  N10: Part3.SCL, Part1.A5/SCL
  N11: S1.leg0, Part1.D4, R1.Pin_1
  N12: S2.leg0, Part1.D5_PWM, R2.Pin_1
  N13: J1.pin2, Part1.D3_PWM

notes:
  unlock
  lock

custom parts:
  SSR-40VA: SSR-40VA solid state relay.
  RFID-RC522-v2: A simple China made RFID-RC522 Reader; do check the pin labels, as this is a MFRC522 based clone.
  LCD1602-I2C: A standard character display, usually with 2x16 characters. Comes in many colors with LCM1602 IIC attached.
